# Fritzing sketch IOTv1 (saved by Fritzing 0.9.1b)
breadboards: 1

parts:
  Part1 = Arduino Uno (Rev3)
  R1 = Photocell (LDR) [package=THT]
  R3 = Resistor [tolerance=±5% resistance=10k package=THT]
  R2 = Trimmer Potentiometer [maximum_resistance=10kΩ package=THT]
  LED1 = RGB LED - (4 legs) [package="5 mm [THT]"]
  R4 = Resistor [tolerance=±5% resistance=220 package=THT]

nets:
  N1: Part1.A0, R1.pin_1, R3.Pin_0
  N2: Part1.A5/SCL, R2.wiper
  N3: Part1.D3_PWM, LED1.red_cathode
  N4: Part1.3V3, R4.Pin_0
  N5: Part1.5V, R3.Pin_1, R2.leg2
  N6: R1.pin_0, R2.leg1
  N7: LED1.common_anode, R4.Pin_1
